# Fritzing sketch MrGibbs (saved by Fritzing 0.9.2b)
breadboards: 1

parts:
  Raspberry_Pi1 = Raspberry Pi 2
  U1 = SUP500F [package=sup500f]
  U2 = ADXL345 [package=lga14]
  Part1 = Triple Axis Magnetometer - HMC5883 Breakout
  Grove1 = Grove OLED 128x96

nets:
  VCC: Raspberry_Pi1.3v3, Raspberry_Pi1.3V3, U1.VCC, U2.VDD, U2.SDO, Part1.VCC, Grove1.VCC
  N1: Raspberry_Pi1.GPIO2, U2.SDA, Part1.SDA, Grove1.SDA
  N2: Raspberry_Pi1.GPIO3, U2.SCL, Part1.SCL, Grove1.SCL
  GND: Raspberry_Pi1.GND, U1.GND, U2.GND, Part1.GND, Grove1.GND
  N3: Raspberry_Pi1.GPIO15, U1.TX-O
  N4: Raspberry_Pi1.GPIO14, U1.RX-I
